# Fritzing sketch IMU (saved by Fritzing 0.9.3b)
breadboards: 1

parts:
  Εξάρτημα1 = Arduino Nano (Rev3.0)
  Εξάρτημα2 = InvenSense MPU6050

nets:
  GND: Εξάρτημα1.GND, Εξάρτημα2.GND
  5V: Εξάρτημα1.5V, Εξάρτημα2.VCC
  N1: Εξάρτημα1.A5, Εξάρτημα2.SCL
  N2: Εξάρτημα1.A4, Εξάρτημα2.SDA
