# Fritzing sketch Motors (saved by Fritzing 0.9.3b)

parts:
  KY-1 = Keyes Relay [package=THT]
  M1 = DC Motor
  M3 = DC Motor
  M2 = DC Motor
  VCC1 = Battery block 9V

nets:
  N1: KY-1.NC, VCC1.-
  N2: KY-1.C, M1.pin_2, M3.pin_2, M2.pin_2

custom parts:
  Keyes Relay: The Keyes 5V relay module is suitable for SCM development, home appliance control. It uses a 5V~12V TIL control signal which can control DC / AC signal.
