# Fritzing sketch Relay (saved by Fritzing 0.9.3b)
breadboards: 1

parts:
  Εξάρτημα1 = Arduino Nano (Rev3.0)
  KY-1 = Keyes Relay [package=THT]

nets:
  N1: Εξάρτημα1.GND, KY-1.ground
  N2: Εξάρτημα1.D2, KY-1.signal
  N3: Εξάρτημα1.5V, KY-1.power

custom parts:
  Keyes Relay: The Keyes 5V relay module is suitable for SCM development, home appliance control. It uses a 5V~12V TIL control signal which can control DC / AC signal.
