# Fritzing sketch controller full (saved by Fritzing 0.9.3b)
breadboards: 1

parts:
  Εξάρτημα1 = Arduino Nano (Rev3.0)
  Εξάρτημα2 = InvenSense MPU6050
  KY-1 = Keyes Relay [package=THT]
  M1 = DC Motor
  M2 = DC Motor
  M3 = DC Motor
  VCC1 = Battery block 9V

nets:
  GND: Εξάρτημα1.GND, Εξάρτημα2.GND, KY-1.ground
  N1: Εξάρτημα1.D2, KY-1.signal
  5V: Εξάρτημα1.5V, Εξάρτημα2.VCC, KY-1.power
  N2: Εξάρτημα1.A5, Εξάρτημα2.SCL
  N3: Εξάρτημα1.A4, Εξάρτημα2.SDA
  N4: KY-1.NC, VCC1.-
  N5: KY-1.C, M1.pin_2, M2.pin_2, M3.pin_2

notes:
  Κινητήρας δόνησης
  Ανεμιστήρας

custom parts:
  Keyes Relay: The Keyes 5V relay module is suitable for SCM development, home appliance control. It uses a 5V~12V TIL control signal which can control DC / AC signal.
